// Logisim project aula1.circ as structural Verilog: 6 circuits, main circuit Decoder3_8
module main (
);

  wire bargraph3_8_1_y0, bargraph3_8_1_y1, bargraph3_8_1_y2, bargraph3_8_1_y3, bargraph3_8_1_y4,
       bargraph3_8_1_y5, bargraph3_8_1_y6, bargraph3_8_1_y7, decoder3_8_1_y0, decoder3_8_1_y1,
       decoder3_8_1_y2, decoder3_8_1_y3, decoder3_8_1_y4, decoder3_8_1_y5, decoder3_8_1_y6, decoder3_8_1_y7,
       multiplex2x8_1_y0, multiplex2x8_1_y1, multiplex2x8_1_y2, multiplex2x8_1_y3, multiplex2x8_1_y4,
       multiplex2x8_1_y5, multiplex2x8_1_y6, multiplex2x8_1_y7, switch_1_p2;
  wire [2:0] slider_1_out;

  // Switch switch_1: pin names not known; wires that end beside it: 1'b0, switch_1_p2
  Slider #(.width(3)) slider_1 (.out(slider_1_out));
  Pull_Resistor #(.pull(1)) pull_resistor_1 (.node(switch_1_p2));
  Decoder3_8 decoder3_8_1 (
    .S0(slider_1_out[0]), .S1(slider_1_out[1]), .S2(slider_1_out[2]), .Y0(decoder3_8_1_y0),
    .Y1(decoder3_8_1_y1), .Y2(decoder3_8_1_y2), .Y3(decoder3_8_1_y3), .Y4(decoder3_8_1_y4),
    .Y5(decoder3_8_1_y5), .Y6(decoder3_8_1_y6), .Y7(decoder3_8_1_y7));
  BarGraph3_8 bargraph3_8_1 (
    .S0(slider_1_out[0]), .S1(slider_1_out[1]), .S2(slider_1_out[2]), .Y0(bargraph3_8_1_y0),
    .Y1(bargraph3_8_1_y1), .Y2(bargraph3_8_1_y2), .Y3(bargraph3_8_1_y3), .Y4(bargraph3_8_1_y4),
    .Y5(bargraph3_8_1_y5), .Y6(bargraph3_8_1_y6), .Y7(bargraph3_8_1_y7));
  Multiplex2x8 multiplex2x8_1 (
    .A0(decoder3_8_1_y0), .B0(bargraph3_8_1_y0), .A1(decoder3_8_1_y1), .B1(bargraph3_8_1_y1),
    .A2(decoder3_8_1_y2), .B2(bargraph3_8_1_y2), .A3(decoder3_8_1_y3), .B3(bargraph3_8_1_y3),
    .A4(decoder3_8_1_y4), .B4(bargraph3_8_1_y4), .A5(decoder3_8_1_y5), .B5(bargraph3_8_1_y5),
    .A6(decoder3_8_1_y6), .B6(bargraph3_8_1_y6), .A7(decoder3_8_1_y7), .B7(bargraph3_8_1_y7),
    .S(switch_1_p2), .Y0(multiplex2x8_1_y0), .Y1(multiplex2x8_1_y1), .Y2(multiplex2x8_1_y2),
    .Y3(multiplex2x8_1_y3), .Y4(multiplex2x8_1_y4), .Y5(multiplex2x8_1_y5), .Y6(multiplex2x8_1_y6),
    .Y7(multiplex2x8_1_y7));
  LED led_1 (.in(multiplex2x8_1_y0));
  LED led_2 (.in(multiplex2x8_1_y1));
  LED led_3 (.in(multiplex2x8_1_y2));
  LED led_4 (.in(multiplex2x8_1_y3));
  LED led_5 (.in(multiplex2x8_1_y4));
  LED led_6 (.in(multiplex2x8_1_y5));
  LED led_7 (.in(multiplex2x8_1_y6));
  LED led_8 (.in(multiplex2x8_1_y7));

  // Notes on the sheet:
  //   Velocidade
  //   BarGraph
endmodule

// Decoder
module Decoder3_8 (
  input  S0,
  input  S1,
  input  S2,
  output Y0,
  output Y1,
  output Y2,
  output Y3,
  output Y4,
  output Y5,
  output Y6,
  output Y7
);

  and P000 (Y0, ~S0, ~S1, ~S2);  // AND_Gate
  and P001 (Y1, S0, ~S1, ~S2);  // AND_Gate
  and P010 (Y2, ~S0, S1, ~S2);  // AND_Gate
  and P011 (Y3, S0, S1, ~S2);  // AND_Gate
  and P100 (Y4, ~S0, ~S1, S2);  // AND_Gate
  and P101 (Y5, S0, ~S1, S2);  // AND_Gate
  and P110 (Y6, ~S0, S1, S2);  // AND_Gate
  and P111 (Y7, S0, S1, S2);
endmodule

// BarGraph
module BarGraph3_8 (
  input  S0,
  input  S1,
  input  S2,
  output Y0,
  output Y1,
  output Y2,
  output Y3,
  output Y4,
  output Y5,
  output Y6,
  output Y7
);

  wire and_1_out, and_3_out;

  and and_1 (and_1_out, S0, S1);
  and and_2 (Y6, S1, S2);
  and and_3 (and_3_out, S0, S2);
  or or_1 (Y1, S0, S1, S2);
  or or_2 (Y2, S1, S2);
  or or_3 (Y3, S2, and_1_out);
  or or_4 (Y5, Y6, and_3_out);
  and and_4 (Y7, S0, S1, S2);
  Pull_Resistor #(.pull(1)) pull_resistor_1 (.node(Y0));

  assign Y4 = S2;
endmodule

module Multiplex2x1 (
  input  E0,
  input  E1,
  input  S,
  output Y
);

  wire and_1_out, and_2_out;

  and and_1 (and_1_out, E0, S);
  and and_2 (and_2_out, E1, ~S);  // AND_Gate
  or or_1 (Y, and_1_out, and_2_out);
endmodule

module Multiplex8x1 (
  input  E0,
  input  E1,
  input  E2,
  input  E3,
  input  E4,
  input  E5,
  input  E6,
  input  E7,
  input  S0,
  input  S1,
  input  S2,
  output Y
);

  wire and_1_out, and_2_out, and_3_out, and_4_out, and_5_out, and_6_out, and_7_out, and_8_out,
       decoder3_8_1_y0, decoder3_8_1_y1, decoder3_8_1_y2, decoder3_8_1_y3, decoder3_8_1_y4, decoder3_8_1_y5,
       decoder3_8_1_y6, decoder3_8_1_y7;

  Decoder3_8 decoder3_8_1 (
    .S0(S0), .S1(S1), .S2(S2), .Y0(decoder3_8_1_y0), .Y1(decoder3_8_1_y1), .Y2(decoder3_8_1_y2),
    .Y3(decoder3_8_1_y3), .Y4(decoder3_8_1_y4), .Y5(decoder3_8_1_y5), .Y6(decoder3_8_1_y6),
    .Y7(decoder3_8_1_y7));
  and and_1 (and_1_out, E0, decoder3_8_1_y0);
  and and_2 (and_2_out, E1, decoder3_8_1_y1);
  and and_3 (and_3_out, E2, decoder3_8_1_y2);
  and and_4 (and_4_out, E3, decoder3_8_1_y3);
  and and_5 (and_5_out, E4, decoder3_8_1_y4);
  and and_6 (and_6_out, E5, decoder3_8_1_y5);
  and and_7 (and_7_out, E6, decoder3_8_1_y6);
  and and_8 (and_8_out, E7, decoder3_8_1_y7);
  or or_1 (Y, and_1_out, and_2_out, and_3_out, and_4_out, and_5_out, and_6_out, and_7_out, and_8_out);
endmodule

module Multiplex2x8 (
  input  A0,
  input  B0,
  input  A1,
  input  B1,
  input  A2,
  input  B2,
  input  A3,
  input  B3,
  input  A4,
  input  B4,
  input  A5,
  input  B5,
  input  A6,
  input  B6,
  input  A7,
  input  B7,
  input  S,
  output Y0,
  output Y1,
  output Y2,
  output Y3,
  output Y4,
  output Y5,
  output Y6,
  output Y7
);

  Multiplex2x1 multiplex2x1_1 (.E0(A0), .E1(B0), .S(S), .Y(Y0));
  Multiplex2x1 multiplex2x1_2 (.E0(A1), .E1(B1), .S(S), .Y(Y1));
  Multiplex2x1 multiplex2x1_3 (.E0(A2), .E1(B2), .S(S), .Y(Y2));
  Multiplex2x1 multiplex2x1_4 (.E0(A3), .E1(B3), .S(S), .Y(Y3));
  Multiplex2x1 multiplex2x1_5 (.E0(A4), .E1(B4), .S(S), .Y(Y4));
  Multiplex2x1 multiplex2x1_6 (.E0(A5), .E1(B5), .S(S), .Y(Y5));
  Multiplex2x1 multiplex2x1_7 (.E0(A6), .E1(B6), .S(S), .Y(Y6));
  Multiplex2x1 multiplex2x1_8 (.E0(A7), .E1(B7), .S(S), .Y(Y7));
endmodule
