// Logisim project aula2.circ as structural Verilog: 3 circuits, main circuit main
module main (
  input  j1,
  input  j2,
  input  j3,
  input  j4
);

  wire and_1_out, and_2_out, and_3_out, and_4_out, and_5_out, and_6_out, not_1_out, or_1_out, or_2_out;

  and and_1 (and_1_out, j1, j2, j3, j4);
  and and_2 (and_2_out, ~j1, ~j2, ~j3, ~j4);  // AND_Gate
  and and_3 (and_3_out, j1, j2, j3);
  and and_4 (and_4_out, j1, j2, j4);
  and and_5 (and_5_out, j1, j3, j4);
  and and_6 (and_6_out, j2, j3, j4);
  or or_1 (or_1_out, and_1_out, and_2_out);
  LED Maioria (.in(or_1_out));
  LED Reprovado (.in(not_1_out));
  not not_1 (not_1_out, or_2_out);
  or or_2 (or_2_out, and_3_out, and_4_out, and_5_out, and_6_out);
  LED Aprovado (.in(or_2_out));
endmodule

module Flags (
  input  [31:0] in_1,
  output Z,
  output N
);

  nor nor_1 (Z, in_1[0], in_1[1], in_1[2], in_1[3], in_1[4], in_1[5], in_1[6], in_1[7], in_1[8], in_1[9], in_1[10], in_1[11], in_1[12], in_1[13], in_1[14], in_1[15], in_1[16], in_1[17], in_1[18], in_1[19], in_1[20], in_1[21], in_1[22], in_1[23], in_1[24], in_1[25], in_1[26], in_1[27], in_1[28], in_1[29], in_1[30], in_1[31]);

  assign N = in_1[31];
endmodule

module ALU (
  input  [2:0] Operacao,
  input  [31:0] A,
  input  [31:0] B,
  output [31:0] out_4
);

  wire [31:0] adder_1_out, and_1_out, and_2_out, bit_extender_1_out, not_1_out, or_1_out, shifter_1_out,
       shifter_2_out, shifter_3_out;

  assign bit_extender_1_out = {{31{Operacao[2]}}, Operacao[2]};  // Bit_Extender bit_extender_1
  Adder #(.width(32)) adder_1 (.a(A), .b(and_1_out), .out(adder_1_out), .cin(Operacao[2]));  // open: cout
  assign and_1_out = ~bit_extender_1_out & B;  // AND_Gate and_1, 32 bits wide
  assign and_2_out = A & B;  // AND_Gate and_2, 32 bits wide
  assign or_1_out = A | B;  // OR_Gate or_1, 32 bits wide
  assign not_1_out = ~A;  // NOT_Gate not_1, 32 bits wide
  Shifter #(.shift("ar"), .width(32)) shifter_1 (.in(A), .\dist (B[4:0]), .out(shifter_1_out));
  Shifter #(.width(32)) shifter_2 (.in(A), .\dist (B[4:0]), .out(shifter_2_out));
  Shifter #(.shift("lr"), .width(32)) shifter_3 (.in(A), .\dist (B[4:0]), .out(shifter_3_out));
  Multiplexer #(.select(3), .width(32)) multiplexer_1 (
    .in0(adder_1_out), .in1(and_2_out), .in2(or_1_out), .in3(not_1_out), .in4(adder_1_out),
    .in5(shifter_1_out), .in6(shifter_2_out), .in7(shifter_3_out), .out(out_4), .sel(Operacao));
endmodule
