// Logisim project aula3.circ as structural Verilog: 3 circuits, main circuit Decodificador
module Decodificador (
  input  b0,
  input  b1,
  output y0,
  output y1,
  output y2,
  output y3
);

  and and_1 (y0, ~b0, ~b1);  // AND_Gate
  and and_2 (y1, b0, ~b1);  // AND_Gate
  and and_3 (y2, ~b0, b1);  // AND_Gate
  and and_4 (y3, b0, b1);

  // Notes on the sheet:
  //   Decodificador como gerador de minTermos
endmodule

module FunctGenerator (
  input  [2:0] Entradas,
  output F
);

  wire decoder_1_out0, decoder_1_out2, decoder_1_out7;

  Decoder #(.enable("false"), .select(3)) decoder_1 (
    .out0(decoder_1_out0), .out2(decoder_1_out2), .out7(decoder_1_out7), .sel(Entradas));  // open: out1, out3, out4, out5, out6
  or or_1 (F, decoder_1_out0, decoder_1_out2, decoder_1_out7);

  // Notes on the sheet:
  //   F = ¬A.¬B.¬C + ¬A.B.¬C + A.B.C
  //   Gerador de Funções Booleanas com Decodificador
endmodule

module MemROM (
  input  a0,
  input  a1,
  output b7,
  output b6,
  output b5,
  output b4,
  output b3,
  output b2,
  output b1,
  output b0
);

  wire and_1_out, and_2_out, and_3_out, and_4_out;

  and and_1 (and_1_out, ~a0, ~a1);  // AND_Gate
  and and_2 (and_2_out, a0, ~a1);  // AND_Gate
  and and_3 (and_3_out, ~a0, a1);  // AND_Gate
  and and_4 (and_4_out, a0, a1);
  Pull_Resistor pull_resistor_1 (.node(and_1_out));
  Pull_Resistor pull_resistor_2 (.node(and_2_out));
  Pull_Resistor pull_resistor_3 (.node(and_3_out));
  Pull_Resistor pull_resistor_4 (.node(and_4_out));
  or or_1 (b7, and_1_out, and_2_out, and_3_out, and_4_out);
  Pull_Resistor pull_resistor_5 (.node(and_1_out));
  Pull_Resistor pull_resistor_6 (.node(and_2_out));
  Pull_Resistor pull_resistor_7 (.node(and_3_out));
  Pull_Resistor pull_resistor_8 (.node(and_4_out));
  Pull_Resistor pull_resistor_9 (.node(and_1_out));
  Pull_Resistor pull_resistor_10 (.node(and_2_out));
  or or_2 (b6, and_1_out, and_2_out, and_3_out, and_4_out);
  Pull_Resistor pull_resistor_11 (.node(and_3_out));
  Pull_Resistor pull_resistor_12 (.node(and_4_out));
  Pull_Resistor pull_resistor_13 (.node(and_1_out));
  Pull_Resistor pull_resistor_14 (.node(and_2_out));
  Pull_Resistor pull_resistor_15 (.node(and_3_out));
  or or_3 (b5, and_1_out, and_2_out, and_3_out, and_4_out);
  or or_4 (b4, and_1_out, and_2_out, and_3_out, and_4_out);
  Pull_Resistor pull_resistor_16 (.node(and_4_out));
  Pull_Resistor pull_resistor_17 (.node(and_1_out));
  Pull_Resistor pull_resistor_18 (.node(and_2_out));
  Pull_Resistor pull_resistor_19 (.node(and_3_out));
  Pull_Resistor pull_resistor_20 (.node(and_4_out));
  or or_5 (b3, and_1_out, and_2_out, and_3_out, and_4_out);
  Pull_Resistor pull_resistor_21 (.node(and_1_out));
  Pull_Resistor pull_resistor_22 (.node(and_2_out));
  Pull_Resistor pull_resistor_23 (.node(and_3_out));
  Pull_Resistor pull_resistor_24 (.node(and_4_out));
  Pull_Resistor pull_resistor_25 (.node(and_1_out));
  Pull_Resistor pull_resistor_26 (.node(and_2_out));
  or or_6 (b2, and_1_out, and_2_out, and_3_out, and_4_out);
  Pull_Resistor pull_resistor_27 (.node(and_3_out));
  Pull_Resistor pull_resistor_28 (.node(and_4_out));
  Pull_Resistor pull_resistor_29 (.node(and_1_out));
  Pull_Resistor pull_resistor_30 (.node(and_2_out));
  Pull_Resistor pull_resistor_31 (.node(and_3_out));
  or or_7 (b1, and_1_out, and_2_out, and_3_out, and_4_out);
  or or_8 (b0, and_1_out, and_2_out, and_3_out, and_4_out);
  Pull_Resistor pull_resistor_32 (.node(and_4_out));
endmodule
