// Logisim project mult.circ as structural Verilog: 2 circuits, main circuit main
module main (
  input  [15:0] Ea,
  input  [15:0] Eb,
  input  Bsel,
  input  [15:0] Z,
  input  Csel,
  input  Reset
);

  wire clock_1_out, not_1_out, not_2_out, or_1_out;
  wire [15:0] A_q, B_q, C_q, multiplexer_1_out, multiplexer_2_out, undriven;

  Multiplexer #(.width(16)) multiplexer_1 (.in0(Eb), .in1(undriven), .out(multiplexer_1_out), .sel(Bsel));
  Multiplexer #(.width(16)) multiplexer_2 (.in0(Z), .in1(undriven), .out(multiplexer_2_out), .sel(Csel));
  Register #(.width(16)) A (.D(Ea), .en(not_1_out), .clk(clock_1_out), .Q(A_q), .clr(Reset));
  not not_1 (not_1_out, not_2_out);
  Register #(.width(16)) B (
    .D(multiplexer_1_out), .en(not_2_out), .clk(clock_1_out), .Q({{8{B_q[15]}}, B_q[7:0]}), .clr(Reset));
  Register #(.width(16)) C (.D(multiplexer_2_out), .en(not_2_out), .clk(clock_1_out), .Q(C_q), .clr(Reset));
  Clock clock_1 (.out(clock_1_out));
  or or_1 (or_1_out, B_q[0], B_q[1], B_q[2], B_q[3], B_q[4], B_q[5], B_q[6], B_q[7], B_q[15], B_q[15], B_q[15], B_q[15], B_q[15], B_q[15], B_q[15], B_q[15]);
  not not_2 (not_2_out, or_1_out);
endmodule

module ula (
  input  [15:0] A,
  input  [15:0] C,
  input  in_3,
  input  in_4
);

  wire [15:0] adder_1_out;

  Adder #(.width(16)) adder_1 (.a(A), .b(C), .out(adder_1_out));  // open: cin, cout
  Subtractor subtractor_1 ();  // open: a, b, out, bin, bout
endmodule
