// Logisim project mult2.circ as structural Verilog: 2 circuits, main circuit main
module main (
  input  [15:0] Ea,
  input  [15:0] Eb,
  input  [15:0] in_3,
  input  Reset,
  input  LOAD,
  output READY,
  output ERROR
);

  wire adder_1_cout, and_1_out, and_2_out, and_3_out, and_4_out, and_5_out, and_6_out, and_7_out,
       clock_1_out, d_ff_1_q, d_ff_2_q, not_1_out, not_2_out, not_3_out, not_4_out, not_5_out, not_6_out,
       not_7_out, not_8_out, not_9_out, or_1_out, or_2_out, or_3_out, or_4_out, or_5_out, xor_1_out;
  wire [15:0] A_q, adder_1_out, B_q, C_q, multiplexer_1_out, multiplexer_2_out, subtractor_1_out;

  Multiplexer #(.width(16)) multiplexer_1 (.in0(Eb), .in1(subtractor_1_out), .out(multiplexer_1_out), .sel(and_7_out));
  Multiplexer #(.width(16)) multiplexer_2 (
    .in0({16{1'b0}}), .in1(adder_1_out), .out(multiplexer_2_out), .sel(and_6_out));
  Register #(.width(16)) A (.D(Ea), .en(and_5_out), .clk(clock_1_out), .Q(A_q), .clr(Reset));
  Register #(.width(16)) B (.D(multiplexer_1_out), .en(d_ff_2_q), .clk(clock_1_out), .Q(B_q), .clr(Reset));
  Register #(.width(16)) C (.D(multiplexer_2_out), .en(xor_1_out), .clk(clock_1_out), .Q(C_q), .clr(Reset));
  Clock clock_1 (.out(clock_1_out));
  or or_1 (or_1_out, B_q[0], B_q[1], B_q[2], B_q[3], B_q[4], B_q[5], B_q[6], B_q[7], B_q[9], B_q[10], B_q[11], B_q[12], B_q[13], B_q[14], B_q[15], B_q[8]);
  Subtractor #(.width(16)) subtractor_1 (.a(B_q), .b(in_3), .out(subtractor_1_out));  // open: bin, bout
  not not_1 (not_1_out, or_1_out);
  Adder #(.width(16)) adder_1 (.a(A_q), .b(C_q), .out(adder_1_out), .cout(adder_1_cout));  // open: cin
  or or_2 (or_2_out, not_1_out, adder_1_cout);
  not not_2 (not_2_out, or_2_out);
  not not_3 (not_3_out, d_ff_1_q);
  not not_4 (not_4_out, d_ff_2_q);
  not not_5 (not_5_out, d_ff_2_q);
  and and_1 (and_1_out, not_3_out, d_ff_2_q);
  and and_2 (and_2_out, not_4_out, d_ff_1_q);
  and and_3 (and_3_out, not_5_out, LOAD);
  and and_4 (and_4_out, not_2_out, d_ff_1_q);
  or or_3 (or_3_out, and_2_out, and_3_out);
  D_Flip_Flop d_ff_1 (.D(or_4_out), .clk(clock_1_out), .Q(d_ff_1_q), .reset(Reset));  // open: Qn, preset
  or or_4 (or_4_out, and_4_out, and_1_out);
  D_Flip_Flop d_ff_2 (.D(or_3_out), .clk(clock_1_out), .Q(d_ff_2_q), .reset(Reset));  // open: Qn, preset
  not not_6 (not_6_out, d_ff_1_q);
  not not_7 (not_7_out, d_ff_2_q);
  and and_5 (and_5_out, not_6_out, d_ff_2_q);
  buf xor_1 (xor_1_out, d_ff_2_q);  // XOR_Gate
  not not_8 (not_8_out, d_ff_2_q);
  not not_9 (not_9_out, d_ff_1_q);
  and and_6 (and_6_out, d_ff_2_q, d_ff_1_q);
  and and_7 (and_7_out, d_ff_1_q, not_7_out);
  or or_5 (or_5_out, d_ff_1_q, d_ff_2_q, adder_1_cout);
  not not_10 (READY, or_5_out);
  and and_8 (ERROR, adder_1_cout, not_8_out, not_9_out);
endmodule

module ula (
  input  [15:0] A,
  input  [15:0] C,
  input  in_3,
  input  in_4
);

  wire [15:0] adder_1_out;

  Adder #(.width(16)) adder_1 (.a(A), .b(C), .out(adder_1_out));  // open: cin, cout
  Subtractor subtractor_1 ();  // open: a, b, out, bin, bout
endmodule
