// Logisim project nsei.circ as structural Verilog: 1 circuit, main circuit main
module main (
  input  in_1,
  input  in_2,
  input  in_3,
  output out_4
);

  wire nand_1_out, nand_2_out, nand_3_out, not_1_out, not_2_out, not_3_out;

  not not_1 (not_1_out, in_1);
  not not_2 (not_2_out, in_2);
  nand nand_1 (nand_1_out, not_1_out, not_2_out);
  not not_3 (not_3_out, in_3);
  nand nand_2 (nand_2_out, not_1_out, in_3);
  nand nand_3 (nand_3_out, in_1, nand_1_out);
  or or_1 (out_4, nand_3_out, nand_2_out);
endmodule
