// Logisim project quest10_3.circ as structural Verilog: 3 circuits, main circuit main
module main (
  input  in_1,
  input  in_2,
  input  in_3,
  input  in_4,
  output out_5,
  output out_6
);

  wire and_1_out, and_2_out, and_3_out, and_4_out, and_5_out, nor_1_out, not_1_out, not_2_out, not_3_out,
       not_4_out, not_5_out, not_6_out, not_8_out, or_1_out, or_2_out, or_3_out;

  not not_1 (not_1_out, in_3);
  not not_2 (not_2_out, in_4);
  or or_1 (or_1_out, in_1, in_2);
  or or_2 (or_2_out, not_1_out, not_2_out);
  not not_3 (not_3_out, in_2);
  not not_4 (not_4_out, in_4);
  nor nor_1 (nor_1_out, in_1, in_2);
  or or_3 (or_3_out, in_3, in_4);
  not not_5 (not_5_out, in_1);
  not not_6 (not_6_out, in_2);
  // NOT_Gate not_7 has open pins: in=in_3, out=open
  not not_8 (not_8_out, in_4);
  and and_1 (and_1_out, nor_1_out, or_3_out);
  and and_2 (and_2_out, in_3, in_4);
  and and_3 (and_3_out, not_5_out, not_6_out, not_8_out);
  and and_4 (and_4_out, or_1_out, not_3_out, not_4_out);
  and and_5 (and_5_out, in_1, or_2_out, in_2);
  or or_4 (out_6, and_1_out, and_2_out, and_3_out);
  or or_5 (out_5, and_4_out, and_5_out);
endmodule

module feita (
  input  a,
  input  b,
  input  c,
  input  d,
  output x,
  output y
);

  wire and_1_out, and_2_out, and_3_out, and_4_out, and_5_out, not_1_out, not_2_out, not_3_out, not_4_out,
       not_5_out, not_6_out, or_1_out, or_2_out, or_3_out, or_4_out;

  not not_1 (not_1_out, a);
  not not_2 (not_2_out, b);
  not not_3 (not_3_out, c);
  not not_4 (not_4_out, d);
  or or_1 (or_1_out, a, b);
  or or_2 (or_2_out, not_3_out, not_4_out);
  not not_5 (not_5_out, a);
  or or_3 (or_3_out, not_5_out, not_6_out);
  not not_6 (not_6_out, b);
  or or_4 (or_4_out, c, d);
  and and_1 (and_1_out, or_1_out, not_3_out, not_4_out);
  and and_2 (and_2_out, a, or_2_out, b);
  and and_3 (and_3_out, or_3_out, or_4_out);
  and and_4 (and_4_out, c, d);
  and and_5 (and_5_out, not_1_out, not_2_out, not_4_out);
  or or_5 (x, and_1_out, and_2_out);
  or or_6 (y, and_3_out, and_4_out, and_5_out);
endmodule

module build (
  input  N,
  input  S,
  input  L,
  input  O,
  output NS,
  output LO
);

  wire and_1_out, and_2_out, and_3_out, and_4_out, and_5_out, not_1_out, not_2_out, not_3_out, not_4_out,
       or_1_out, or_2_out, or_3_out, or_4_out;

  not not_1 (not_1_out, N);
  not not_2 (not_2_out, S);
  not not_3 (not_3_out, L);
  not not_4 (not_4_out, O);
  or or_1 (or_1_out, N, S);
  or or_2 (or_2_out, not_3_out, not_4_out);
  or or_3 (or_3_out, not_1_out, not_2_out);
  or or_4 (or_4_out, L, O);
  and and_1 (and_1_out, or_1_out, not_3_out, not_4_out);
  and and_2 (and_2_out, N, or_2_out, S);
  and and_3 (and_3_out, or_3_out, or_4_out);
  and and_4 (and_4_out, L, O);
  and and_5 (and_5_out, not_1_out, not_2_out, not_4_out);
  or or_5 (NS, and_1_out, and_2_out);
  or or_6 (LO, and_3_out, and_4_out, and_5_out);
endmodule
